# Fritzing sketch esquemafzz (saved by Fritzing 0.9.9b)

parts:
  Componente1 = Arduino Nano (Rev3.0)
  Componente2 = Arduino GSM Shield
  VCC1 = Battery
  R1 = Resistor [tolerance=±5% resistance=10k power=0.25 package=THT]
  S1 = Toggle Switch [package=THT]

nets:
  N1: Componente1.D3, Componente2.RST_MDM/D7
  N2: Componente1.D5, Componente2.D8
  N3: Componente1.D6, Componente2.PWM_D9
  VIN: Componente1.VIN, Componente2.5V, S1.L1
  N4: Componente1.GND, VCC1.-, R1.Pin_0
  N5: VCC1.+, S1.COM

notes:
  +4.5V
  10k
  7.4V
  Vin

custom parts:
  Battery: Your standard 2x 18650 battery pack (7,4 Volts)
